// Logisim project AMB.circ as structural Verilog: 7 circuits, main circuit mips
module alu (
  input  [2:0] ALU_Control,
  input  [27:0] in_2,
  input  [27:0] in_3,
  output [27:0] out_4,
  output Zero
);

  wire comparator_1_lt;
  wire [27:0] adder_1_out, and_1_out, multiplexer_1_out, not_1_out, or_1_out, shifter_1_out,
       subtractor_1_out, xor_1_out;

  assign and_1_out = in_2 & in_3;  // AND_Gate and_1, 28 bits wide
  assign or_1_out = in_2 | in_3;  // OR_Gate or_1, 28 bits wide
  Adder #(.width(28)) adder_1 (.a(in_2), .b(in_3), .out(adder_1_out));  // open: cin, cout
  Subtractor #(.width(28)) subtractor_1 (.a(in_2), .b(in_3), .out(subtractor_1_out));  // open: bin, bout
  Comparator #(.width(28), .mode("unsigned")) comparator_1 (.a(in_2), .b(in_3), .lt(comparator_1_lt));  // open: gt, eq
  assign xor_1_out = in_2 ^ in_3;  // XOR_Gate xor_1, 28 bits wide
  assign not_1_out = ~in_2;  // NOT_Gate not_1, 28 bits wide
  Multiplexer #(.width(28), .enable("false")) multiplexer_1 (
    .in0({28{1'b0}}), .in1(28'h1), .out(multiplexer_1_out), .sel(comparator_1_lt));
  Shifter #(.width(28)) shifter_1 (.in(in_2), .\dist (in_3[4:0]), .out(shifter_1_out));
  Multiplexer #(.select(3), .width(28), .disabled(0), .enable("false")) multiplexer_2 (
    .in0(not_1_out), .in1(or_1_out), .in2(and_1_out), .in3(xor_1_out), .in4(shifter_1_out),
    .in5(adder_1_out), .in6(subtractor_1_out), .in7(in_3), .out(out_4), .sel(ALU_Control));
  Comparator #(.width(28), .mode("unsigned")) comparator_2 (.a(out_4), .b({28{1'b0}}), .eq(Zero));  // open: gt, lt

  // Notes on the sheet:
  //   A
  //   B
  //   Logic from the first table in Chapter 4.4
  //   Op selects the result
  //   Output
endmodule

module mips (
);

  wire alu_1_zero, and_1_out, clock_1_out, control_1_alusrc, control_1_branch, control_1_jump,
       control_1_load, control_1_memread, control_1_memwrite, control_1_regdst, control_1_regwrite,
       not_1_out, Restart_Program_out, Zero_Reg_File_out;
  wire [2:0] control_1_aluop;
  wire [3:0] multiplexer_1_out, rom_1_data_2;
  wire [4:0] bit_extender_1_out, bit_extender_3_out;
  wire [10:0] rom_1_data, shifter_1_out;
  wire [27:0] adder_1_out, adder_2_out, adder_3_out, alu_1_out_4, bit_extender_2_out, bit_extender_4_out,
       bit_extender_6_out, bit_extender_7_out, bit_extender_8_out, bit_extender_9_out, multiplexer_4_out,
       multiplexer_5_out, multiplexer_6_out, multiplexer_7_out, multiplexer_8_out, PC_q, ram_1_data;
  wire [31:0] bit_extender_5_out, multiplexer_2_out, multiplexer_3_out, reg_32_1_compa, reg_32_1_compb,
       reg_32_1_jmpoff, reg_32_1_memoff, reg_32_1_readdata1, reg_32_1_readdata2;

  Register #(.width(28)) PC (
    .D(multiplexer_6_out), .Q(PC_q), .clk(clock_1_out), .clr(Restart_Program_out));  // open: en
  Clock clock_1 (.out(clock_1_out));
  Button Restart_Program (.out(Restart_Program_out));
  Button Zero_Reg_File (.out(Zero_Reg_File_out));
  Adder #(.width(28)) adder_1 (.a(PC_q), .b(28'h2), .out(adder_1_out));  // open: cin, cout
  // Probe on shifter_1_out
  // Probe on {rom_1_data_2, rom_1_data}
  ROM #(.addrWidth(10), .dataWidth(15)) rom_1 (.addr(PC_q[10:1]), .data({rom_1_data_2, rom_1_data}));  // open: sel
  alu_control alu_control_1 ();  // open: Operation, ALUOp, Function
  Shifter #(.width(11)) shifter_1 (.in(rom_1_data), .\dist (4'b0001), .out(shifter_1_out));
  not not_1 (not_1_out, control_1_regdst);
  Multiplexer #(.width(4), .disabled(0), .enable("false")) multiplexer_1 (
    .in0(rom_1_data[7:4]), .in1({rom_1_data_2[0], rom_1_data[10:8]}), .out(multiplexer_1_out), .sel(not_1_out));
  assign bit_extender_1_out = {{1{1'b0}}, rom_1_data[3:0]};  // Bit_Extender bit_extender_1
  assign bit_extender_2_out = {{17{shifter_1_out[10]}}, shifter_1_out};  // Bit_Extender bit_extender_2
  assign bit_extender_3_out = {{1{1'b0}}, multiplexer_1_out};  // Bit_Extender bit_extender_3
  // Probe on bit_extender_5_out
  control control_1 (
    .in_1({rom_1_data_2, rom_1_data[10:8]}), .RegDst(control_1_regdst), .Branch(control_1_branch),
    .MemRead(control_1_memread), .ALUOp(control_1_aluop), .MemWrite(control_1_memwrite),
    .ALUSrc(control_1_alusrc), .RegWrite(control_1_regwrite), .load(control_1_load), .JUMP(control_1_jump));  // open: MemtoReg, in_2
  reg_32 reg_32_1 (
    .ReadReg1(bit_extender_3_out), .ReadReg2(bit_extender_1_out), .WriteReg(bit_extender_3_out),
    .RegWrite(control_1_regwrite), .ReadData1(reg_32_1_readdata1), .ReadData2(reg_32_1_readdata2),
    .WriteData(bit_extender_5_out), .Clk(clock_1_out), .Reset(Zero_Reg_File_out), .JMPOFF(reg_32_1_jmpoff),
    .MEMOFF(reg_32_1_memoff), .COMPA(reg_32_1_compa), .COMPB(reg_32_1_compb));  // open: LC
  // Probe on bit_extender_3_out
  // Probe on bit_extender_1_out
  // Probe on bit_extender_3_out
  assign bit_extender_4_out = {{20{rom_1_data[7]}}, rom_1_data[7:0]};  // Bit_Extender bit_extender_4
  assign bit_extender_5_out = {{4{multiplexer_7_out[27]}}, multiplexer_7_out};  // Bit_Extender bit_extender_5
  Bit_Extender #(.in_width(32), .out_width(28), .\type ("sign")) bit_extender_6 (
    .in(reg_32_1_jmpoff), .out(bit_extender_6_out));
  Adder #(.width(28)) adder_2 (.a(bit_extender_2_out), .b(bit_extender_6_out), .out(adder_2_out));  // open: cin, cout
  Multiplexer #(.width(32), .enable("false")) multiplexer_2 (
    .in0(reg_32_1_readdata1), .in1(reg_32_1_compa), .out(multiplexer_2_out), .sel(control_1_branch));
  Multiplexer #(.width(32), .enable("false")) multiplexer_3 (
    .in0(reg_32_1_readdata2), .in1(reg_32_1_compb), .out(multiplexer_3_out), .sel(control_1_branch));
  Bit_Extender #(.in_width(32), .out_width(28), .\type ("sign")) bit_extender_7 (
    .in(reg_32_1_memoff), .out(bit_extender_7_out));
  // Probe on bit_extender_4_out
  Multiplexer #(.width(28), .enable("false")) multiplexer_4 (
    .in0(adder_1_out), .in1(adder_2_out), .out(multiplexer_4_out), .sel(control_1_jump));
  Bit_Extender #(.in_width(32), .out_width(28), .\type ("sign")) bit_extender_8 (
    .in(multiplexer_2_out), .out(bit_extender_8_out));
  Bit_Extender #(.in_width(32), .out_width(28), .\type ("sign")) bit_extender_9 (
    .in(multiplexer_3_out), .out(bit_extender_9_out));
  // Probe on control_1_aluop
  alu alu_1 (
    .out_4(alu_1_out_4), .Zero(alu_1_zero), .in_2(bit_extender_8_out), .in_3(multiplexer_5_out),
    .ALU_Control(control_1_aluop));
  // Probe on bit_extender_8_out
  // Probe on multiplexer_5_out
  Multiplexer #(.width(28), .enable("false")) multiplexer_5 (
    .in0(bit_extender_9_out), .in1(bit_extender_4_out), .out(multiplexer_5_out), .sel(control_1_alusrc));
  Multiplexer #(.width(28), .enable("false")) multiplexer_6 (
    .in0(multiplexer_4_out), .in1(adder_2_out), .out(multiplexer_6_out), .sel(and_1_out));
  and and_1 (and_1_out, control_1_branch, alu_1_zero);
  Multiplexer #(.width(28), .enable("false")) multiplexer_7 (
    .in0(multiplexer_8_out), .in1(ram_1_data), .out(multiplexer_7_out), .sel(control_1_memread));
  Multiplexer #(.width(28), .enable("false")) multiplexer_8 (
    .in0(alu_1_out_4), .in1(multiplexer_5_out), .out(multiplexer_8_out), .sel(control_1_load));
  // Probe on multiplexer_7_out
  // Probe on multiplexer_6_out
  Adder #(.width(28)) adder_3 (.a(bit_extender_7_out), .b(bit_extender_4_out), .out(adder_3_out));  // open: cin, cout
  // Probe on adder_3_out[11:2]
  RAM #(.addrWidth(10), .dataWidth(28), .bus("separate")) ram_1 (
    .addr(adder_3_out[11:2]), .din(multiplexer_8_out), .data(ram_1_data), .str(control_1_memwrite),
    .clk(clock_1_out), .ld(control_1_memread));  // open: sel, clr

  // Notes on the sheet:
  //   Your name and date: 
  //   Clock
  //   Current Instruction
  //   contents of rom_1 (hex, n*v repeats v):
  //   4000 4201 4a05 4d00 4700 4400 460e 1846 19c4 6100 1701 17d2 18a4 19ea 19f7 3002 2800 4d00 7005
  //   Reg Write Data
  //   Imm. Value
  //   ALU Op
  //   Next PC
  //   Mem Addr
  //   Right-click and load the 1234.mem into the RAM.
endmodule

module instruction_type_decode (
  input  [6:0] opcode,
  output NOT,
  output OR,
  output AND,
  output out_5,
  output out_6,
  output out_7,
  output out_8,
  output out_9,
  output out_10,
  output out_11,
  output out_12,
  output out_13,
  output out_14,
  output out_15,
  output out_16,
  output out_17,
  output out_18,
  output out_19,
  output out_20,
  output out_21
);

  wire [6:0] shifter_1_out, shifter_2_out, shifter_3_out, shifter_4_out, shifter_5_out, shifter_6_out,
       shifter_7_out, shifter_8_out;

  Shifter #(.width(7), .shift("lr")) shifter_1 (.in(opcode), .\dist (3'b011), .out(shifter_1_out));
  Shifter #(.width(7), .shift("lr")) shifter_2 (.in(opcode), .\dist (3'b011), .out(shifter_2_out));
  Shifter #(.width(7), .shift("lr")) shifter_3 (.in(opcode), .\dist (3'b011), .out(shifter_3_out));
  Shifter #(.width(7), .shift("lr")) shifter_4 (.in(opcode), .\dist (3'b011), .out(shifter_4_out));
  Shifter #(.width(7), .shift("lr")) shifter_5 (.in(opcode), .\dist (3'b100), .out(shifter_5_out));
  Shifter #(.width(7), .shift("lr")) shifter_6 (.in(opcode), .\dist (3'b100), .out(shifter_6_out));
  Shifter #(.width(7), .shift("lr")) shifter_7 (.in(opcode), .\dist (3'b100), .out(shifter_7_out));
  Shifter #(.width(7), .shift("lr")) shifter_8 (.in(opcode), .\dist (3'b100), .out(shifter_8_out));
  Comparator #(.width(7), .mode("unsigned")) comparator_1 (.a(7'b0010000), .b(opcode), .eq(NOT));  // open: gt, lt
  Comparator #(.width(7), .mode("unsigned")) comparator_2 (.a(7'b0010001), .b(opcode), .eq(OR));  // open: gt, lt
  Comparator #(.width(7), .mode("unsigned")) comparator_3 (.a(7'b0010010), .b(opcode), .eq(AND));  // open: gt, lt
  Comparator #(.width(7), .mode("unsigned")) comparator_4 (.a(7'b0010011), .b(opcode), .eq(out_5));  // open: gt, lt
  Comparator #(.width(7), .mode("unsigned")) comparator_5 (.a(7'b0010100), .b(opcode), .eq(out_6));  // open: gt, lt
  Comparator #(.width(7), .mode("unsigned")) comparator_6 (.a(7'b0010101), .b(opcode), .eq(out_7));  // open: gt, lt
  Comparator #(.width(7), .mode("unsigned")) comparator_7 (.a(7'b0010110), .b(opcode), .eq(out_8));  // open: gt, lt
  Comparator #(.width(7), .mode("unsigned")) comparator_8 (.a(7'b0010111), .b(opcode), .eq(out_9));  // open: gt, lt
  Comparator #(.width(7), .mode("unsigned")) comparator_9 (.a(7'b0011000), .b(opcode), .eq(out_10));  // open: gt, lt
  Comparator #(.width(7), .mode("unsigned")) comparator_10 (.a(7'b0011001), .b(opcode), .eq(out_11));  // open: gt, lt
  Comparator #(.width(7), .mode("unsigned")) comparator_11 (
    .a(7'b0000100), .b(shifter_1_out), .eq(out_12));  // open: gt, lt
  Comparator #(.width(7), .mode("unsigned")) comparator_12 (
    .a(7'b0000101), .b(shifter_2_out), .eq(out_13));  // open: gt, lt
  Comparator #(.width(7), .mode("unsigned")) comparator_13 (
    .a(7'b0000110), .b(shifter_3_out), .eq(out_14));  // open: gt, lt
  Comparator #(.width(7), .mode("unsigned")) comparator_14 (
    .a(7'b0000111), .b(shifter_4_out), .eq(out_15));  // open: gt, lt
  Comparator #(.width(7), .mode("unsigned")) comparator_15 (
    .a(7'b0000100), .b(shifter_5_out), .eq(out_16));  // open: gt, lt
  Comparator #(.width(7), .mode("unsigned")) comparator_16 (
    .a(7'b0000101), .b(shifter_6_out), .eq(out_17));  // open: gt, lt
  Comparator #(.width(7), .mode("unsigned")) comparator_17 (
    .a(7'b0000110), .b(shifter_7_out), .eq(out_18));  // open: gt, lt
  Comparator #(.width(7), .mode("unsigned")) comparator_18 (
    .a(7'b0000111), .b(shifter_8_out), .eq(out_19));  // open: gt, lt
  Comparator #(.width(7), .mode("unsigned")) comparator_19 (.a({7{1'b0}}), .b(opcode), .eq(out_20));  // open: gt, lt
  Comparator #(.width(7), .mode("unsigned")) comparator_20 (.a(7'b0000001), .b(opcode), .eq(out_21));  // open: gt, lt

  // Notes on the sheet:
  //   This example sets "R-format" to true if opcode=00.
  //   ToDo: Fill in the logic from Fig 4.22 to determine the instruction type
  //   Hint: Use comparators and a constant to check for the right values
endmodule

// load
module control_decode (
  input  NOT,
  input  OR,
  input  AND,
  input  XOR,
  input  SHL,
  input  SHR,
  input  SAR,
  input  ADD,
  input  SUB,
  input  MOV,
  input  JMP,
  input  JMPL,
  input  JPEQ,
  input  JPBLW,
  input  LI,
  input  LIHI,
  input  LOAD,
  input  STOR,
  input  HLT,
  input  NOP,
  output ALUSrc,
  output RegDst,
  output MemtoReg,
  output RegWrite,
  output MemRead,
  output load_2,
  output MemWrite,
  output Branch,
  output JUMP,
  output ALUOp1,
  output ALUOp0,
  output ALUOp2
);

  or or_1 (RegWrite, NOT, OR, AND, XOR, SHL, SHR, LOAD, SAR, ADD, SUB, MOV, LI, LIHI);
  or or_2 (ALUSrc, LI, LIHI, LOAD, STOR);
  or or_3 (Branch, JPEQ, JPBLW);
  or or_4 (ALUOp1, MOV, XOR, JPEQ, AND, SUB);
  or or_5 (ALUOp0, MOV, OR, XOR, ADD);
  or or_6 (ALUOp2, MOV, SHL, JPEQ, ADD, SUB);
  or or_7 (load_2, LI, LIHI);
  or or_8 (JUMP, JMP, JMPL);
  or or_9 (RegDst, SUB, NOT, OR, AND, XOR, SHL, SHR, MOV, SAR, ADD);

  assign MemRead = LOAD;
  assign MemtoReg = LOAD;
  assign MemWrite = STOR;
endmodule

module alu_control (
  input  [5:0] Function,
  input  [2:0] ALUOp,
  output [3:0] Operation
);

  wire and_1_out, and_2_out, not_1_out, not_2_out, not_3_out, not_4_out, not_5_out, not_6_out, not_7_out,
       or_1_out, undriven, undriven_2, undriven_3, undriven_4;
  wire [2:0] priority_encoder_1_out;

  not not_1 (not_1_out, ALUOp[2]);
  not not_2 (not_2_out, ALUOp[1]);
  not not_3 (not_3_out, ALUOp[1]);
  not not_4 (not_4_out, Function[3]);
  not not_5 (not_5_out, Function[2]);
  not not_6 (not_6_out, Function[1]);
  not not_7 (not_7_out, Function[0]);
  and and_1 (and_1_out, not_1_out, not_2_out);
  and and_2 (and_2_out, ALUOp[2], not_3_out, not_4_out, not_5_out, not_6_out, not_7_out);
  or or_1 (or_1_out, and_1_out, and_2_out);
  Priority_Encoder priority_encoder_1 (
    .in0(undriven), .in1(undriven_2), .in2(or_1_out), .in3(undriven_4), .in4(undriven_3),
    .out(priority_encoder_1_out));  // open: in5, in6, in7, en_in, gs, en_out
  Multiplexer #(.select(3), .width(4)) multiplexer_1 (
    .in0(4'b0000), .in1(4'b0001), .in2(4'b0010), .in3(4'b0110), .in4(4'b0111), .out(Operation),
    .sel(priority_encoder_1_out));  // open: in5, in6, in7, en

  // Notes on the sheet:
  //   Inputs
  //   B -- OR
  //   ToDo: Fill in logic from Fig 4.13
  //   Hint: Here is the logic for the first row: 
  //   A -- if (ALUOp1=0 and ALUOp0=0)
  //   D -- then output = 2 = 0010
  //   A
  //   C
  //   C -- if (ALUOp1=1 and ALUOp0=0 and F3, F2, F1, F0 are all 0)
  //   B
  //   True for 0010=2
  //   True for 0110=6
  //   True for 0001=1
  //   True for 0111=7
  //   True for 0000=0
  //   We have 5 possible outputs
  //   D
  //   Depending on which input is 1,
  //   one of the outputs above will be selected.
endmodule

module control (
  input  [6:0] in_1,
  input  in_2,
  output RegDst,
  output Branch,
  output MemRead,
  output MemtoReg,
  output [2:0] ALUOp,
  output MemWrite,
  output ALUSrc,
  output RegWrite,
  output load,
  output JUMP
);

  wire instruction_type_decode_1_and, instruction_type_decode_1_not, instruction_type_decode_1_or,
       instruction_type_decode_1_out_5, instruction_type_decode_1_out_6, instruction_type_decode_1_out_7,
       instruction_type_decode_1_out_8, instruction_type_decode_1_out_9, instruction_type_decode_1_out_10,
       instruction_type_decode_1_out_11, instruction_type_decode_1_out_12, instruction_type_decode_1_out_13,
       instruction_type_decode_1_out_14, instruction_type_decode_1_out_15, instruction_type_decode_1_out_16,
       instruction_type_decode_1_out_17, instruction_type_decode_1_out_18, instruction_type_decode_1_out_19,
       instruction_type_decode_1_out_20, instruction_type_decode_1_out_21;

  instruction_type_decode instruction_type_decode_1 (
    .opcode(in_1), .NOT(instruction_type_decode_1_not), .out_6(instruction_type_decode_1_out_6),
    .OR(instruction_type_decode_1_or), .out_7(instruction_type_decode_1_out_7),
    .out_5(instruction_type_decode_1_out_5), .out_8(instruction_type_decode_1_out_8),
    .AND(instruction_type_decode_1_and), .out_9(instruction_type_decode_1_out_9),
    .out_10(instruction_type_decode_1_out_10), .out_11(instruction_type_decode_1_out_11),
    .out_12(instruction_type_decode_1_out_12), .out_13(instruction_type_decode_1_out_13),
    .out_14(instruction_type_decode_1_out_14), .out_15(instruction_type_decode_1_out_15),
    .out_16(instruction_type_decode_1_out_16), .out_17(instruction_type_decode_1_out_17),
    .out_18(instruction_type_decode_1_out_18), .out_19(instruction_type_decode_1_out_19),
    .out_20(instruction_type_decode_1_out_20), .out_21(instruction_type_decode_1_out_21));
  control_decode control_decode_1 (
    .AND(instruction_type_decode_1_and), .XOR(instruction_type_decode_1_out_5),
    .SHL(instruction_type_decode_1_out_6), .SHR(instruction_type_decode_1_out_7), .RegDst(RegDst),
    .ALUSrc(ALUSrc), .MemtoReg(MemtoReg), .RegWrite(RegWrite), .MemRead(MemRead), .MemWrite(MemWrite),
    .Branch(Branch), .ALUOp1(ALUOp[1]), .ALUOp0(ALUOp[0]), .SAR(instruction_type_decode_1_out_8),
    .ADD(instruction_type_decode_1_out_9), .SUB(instruction_type_decode_1_out_10),
    .MOV(instruction_type_decode_1_out_11), .JMP(instruction_type_decode_1_out_12),
    .JMPL(instruction_type_decode_1_out_13), .JPEQ(instruction_type_decode_1_out_14),
    .JPBLW(instruction_type_decode_1_out_15), .LI(instruction_type_decode_1_out_16),
    .LIHI(instruction_type_decode_1_out_17), .LOAD(instruction_type_decode_1_out_18),
    .STOR(instruction_type_decode_1_out_19), .HLT(instruction_type_decode_1_out_20),
    .NOP(instruction_type_decode_1_out_21), .NOT(instruction_type_decode_1_not),
    .OR(instruction_type_decode_1_or), .ALUOp2(ALUOp[2]), .load_2(load), .JUMP(JUMP));

  // Notes on the sheet:
  //   Decode the Instruction Type first
  //   Instruction OpCode
  //   From the Insturction Type,
  //   decode the control signals
endmodule

module reg_32 (
  input  [4:0] ReadReg1,
  input  [4:0] ReadReg2,
  input  [4:0] WriteReg,
  input  RegWrite,
  input  [31:0] WriteData,
  input  Clk,
  input  Reset,
  output [31:0] LC,
  output [31:0] JMPOFF,
  output [31:0] MEMOFF,
  output [31:0] COMPA,
  output [31:0] COMPB,
  output [31:0] ReadData1,
  output [31:0] ReadData2
);

  wire decoder_1_out0, decoder_1_out1, decoder_2_out0, decoder_2_out1, decoder_2_out2, decoder_2_out3,
       decoder_3_out0, decoder_3_out1, decoder_3_out2, decoder_3_out3, decoder_4_out0, decoder_4_out1,
       decoder_4_out2, decoder_4_out3, decoder_5_out0, decoder_5_out1, decoder_5_out2, decoder_5_out3,
       decoder_6_out0, decoder_6_out1, decoder_6_out2, decoder_6_out3, decoder_7_out0, decoder_7_out1,
       decoder_7_out2, decoder_7_out3, decoder_8_out0, decoder_8_out1, decoder_8_out2, decoder_8_out3,
       decoder_9_out0, decoder_9_out1, decoder_9_out2, decoder_9_out3, decoder_10_out0, decoder_10_out1,
       decoder_10_out2, decoder_10_out3, decoder_11_out0, decoder_11_out1, decoder_11_out2, decoder_11_out3;
  wire [31:0] multiplexer_1_out, multiplexer_2_out, multiplexer_3_out, multiplexer_4_out, multiplexer_5_out,
       multiplexer_6_out, multiplexer_7_out, multiplexer_8_out, multiplexer_9_out, multiplexer_10_out,
       multiplexer_13_out, multiplexer_14_out, multiplexer_15_out, multiplexer_16_out, multiplexer_17_out,
       multiplexer_18_out, multiplexer_19_out, multiplexer_20_out, multiplexer_21_out, multiplexer_22_out,
       register_1_q, register_2_q, register_3_q, register_4_q, register_5_q, register_6_q, register_7_q,
       register_8_q, register_10_q, register_11_q, register_16_q, register_17_q, register_18_q,
       register_19_q, register_20_q, register_21_q, register_22_q, register_23_q, register_24_q,
       register_25_q, register_26_q, register_27_q, register_28_q, register_29_q, register_30_q,
       register_31_q;

  // Probe on WriteReg
  Decoder #(.disabled(0)) decoder_1 (.out0(decoder_1_out0), .out1(decoder_1_out1), .sel(WriteReg[4]), .en(RegWrite));
  Decoder #(.select(2), .disabled(0)) decoder_2 (
    .out0(decoder_2_out0), .out1(decoder_2_out1), .out2(decoder_2_out2), .out3(decoder_2_out3),
    .sel(WriteReg[3:2]), .en(decoder_1_out0));
  Decoder #(.select(2), .disabled(0)) decoder_3 (
    .out0(decoder_3_out0), .out1(decoder_3_out1), .out2(decoder_3_out2), .out3(decoder_3_out3),
    .sel(WriteReg[1:0]), .en(decoder_2_out0));
  Decoder #(.select(2), .disabled(0)) decoder_4 (
    .out0(decoder_4_out0), .out1(decoder_4_out1), .out2(decoder_4_out2), .out3(decoder_4_out3),
    .sel(WriteReg[1:0]), .en(decoder_2_out1));
  Decoder #(.select(2), .disabled(0)) decoder_5 (
    .out0(decoder_5_out0), .out1(decoder_5_out1), .out2(decoder_5_out2), .out3(decoder_5_out3),
    .sel(WriteReg[1:0]), .en(decoder_2_out2));
  Decoder #(.select(2), .disabled(0)) decoder_6 (
    .out0(decoder_6_out0), .out1(decoder_6_out1), .out2(decoder_6_out2), .out3(decoder_6_out3),
    .sel(WriteReg[1:0]), .en(decoder_2_out3));
  Register #(.width(32)) register_1 (.D(WriteData), .en(decoder_3_out1), .Q(register_1_q), .clk(Clk), .clr(Reset));
  Register #(.width(32)) register_2 (.D(WriteData), .en(decoder_3_out2), .Q(register_2_q), .clk(Clk), .clr(Reset));
  Register #(.width(32)) register_3 (.D(WriteData), .en(decoder_3_out3), .Q(register_3_q), .clk(Clk), .clr(Reset));
  Register #(.width(32)) register_4 (.D(WriteData), .en(decoder_4_out0), .Q(register_4_q), .clk(Clk), .clr(Reset));
  Register #(.width(32)) register_5 (.D(WriteData), .en(decoder_4_out1), .Q(register_5_q), .clk(Clk), .clr(Reset));
  Register #(.width(32)) register_6 (.D(WriteData), .en(decoder_4_out2), .Q(register_6_q), .clk(Clk), .clr(Reset));
  Register #(.width(32)) register_7 (.D(WriteData), .en(decoder_4_out3), .Q(register_7_q), .clk(Clk), .clr(Reset));
  Register #(.width(32)) register_8 (.D(WriteData), .en(decoder_5_out0), .Q(register_8_q), .clk(Clk), .clr(Reset));
  Register #(.width(32)) register_9 (.D(WriteData), .en(decoder_5_out1), .Q(LC), .clk(Clk), .clr(Reset));
  Register #(.width(32)) register_10 (.D(WriteData), .en(decoder_5_out2), .Q(register_10_q), .clk(Clk), .clr(Reset));
  Register #(.width(32)) register_11 (.D(WriteData), .en(decoder_5_out3), .Q(register_11_q), .clk(Clk), .clr(Reset));
  Register #(.width(32)) register_12 (.D(WriteData), .en(decoder_6_out0), .Q(JMPOFF), .clk(Clk), .clr(Reset));
  Register #(.width(32)) register_13 (.D(WriteData), .en(decoder_6_out1), .Q(MEMOFF), .clk(Clk), .clr(Reset));
  Register #(.width(32)) register_14 (.D(WriteData), .en(decoder_6_out2), .Q(COMPA), .clk(Clk), .clr(Reset));
  Register #(.width(32)) register_15 (.D(WriteData), .en(decoder_6_out3), .Q(COMPB), .clk(Clk), .clr(Reset));
  // Probe on {32{1'b0}}
  // Probe on register_1_q
  // Probe on register_2_q
  // Probe on register_3_q
  // Probe on register_4_q
  // Probe on register_5_q
  // Probe on register_6_q
  // Probe on register_7_q
  // Probe on register_8_q
  // Probe on LC
  // Probe on register_10_q
  // Probe on register_11_q
  // Probe on JMPOFF
  // Probe on MEMOFF
  // Probe on COMPA
  // Probe on COMPB
  // Probe on ReadReg1
  Multiplexer #(.select(2), .width(32), .enable("false")) multiplexer_1 (
    .in0({32{1'b0}}), .in1(register_1_q), .in2(register_2_q), .in3(register_3_q), .out(multiplexer_1_out),
    .sel(ReadReg1[1:0]));
  Multiplexer #(.select(2), .width(32), .enable("false")) multiplexer_2 (
    .in0(register_4_q), .in1(register_5_q), .in2(register_6_q), .in3(register_7_q), .out(multiplexer_2_out),
    .sel(ReadReg1[1:0]));
  Multiplexer #(.select(2), .width(32), .enable("false")) multiplexer_3 (
    .in0(register_8_q), .in1(LC), .in2(register_10_q), .in3(register_11_q), .out(multiplexer_3_out),
    .sel(ReadReg1[1:0]));
  Multiplexer #(.select(2), .width(32), .enable("false")) multiplexer_4 (
    .in0(JMPOFF), .in1(MEMOFF), .in2(COMPA), .in3(COMPB), .out(multiplexer_4_out), .sel(ReadReg1[1:0]));
  // Probe on ReadReg2
  Multiplexer #(.select(2), .width(32), .enable("false")) multiplexer_5 (
    .in0({32{1'b0}}), .in1(register_1_q), .in2(register_2_q), .in3(register_3_q), .out(multiplexer_5_out),
    .sel(ReadReg2[1:0]));
  Multiplexer #(.select(2), .width(32), .enable("false")) multiplexer_6 (
    .in0(register_4_q), .in1(register_5_q), .in2(register_6_q), .in3(register_7_q), .out(multiplexer_6_out),
    .sel(ReadReg2[1:0]));
  Multiplexer #(.select(2), .width(32), .enable("false")) multiplexer_7 (
    .in0(register_8_q), .in1(LC), .in2(register_10_q), .in3(register_11_q), .out(multiplexer_7_out),
    .sel(ReadReg2[1:0]));
  Multiplexer #(.select(2), .width(32), .enable("false")) multiplexer_8 (
    .in0(JMPOFF), .in1(MEMOFF), .in2(COMPA), .in3(COMPB), .out(multiplexer_8_out), .sel(ReadReg2[1:0]));
  Multiplexer #(.select(2), .width(32), .enable("false")) multiplexer_9 (
    .in0(multiplexer_5_out), .in1(multiplexer_6_out), .in2(multiplexer_7_out), .in3(multiplexer_8_out),
    .out(multiplexer_9_out), .sel(ReadReg2[3:2]));
  Multiplexer #(.select(2), .width(32), .enable("false")) multiplexer_10 (
    .in0(multiplexer_1_out), .in1(multiplexer_2_out), .in2(multiplexer_3_out), .in3(multiplexer_4_out),
    .out(multiplexer_10_out), .sel(ReadReg1[3:2]));
  Decoder #(.select(2), .disabled(0)) decoder_7 (
    .out0(decoder_7_out0), .out1(decoder_7_out1), .out2(decoder_7_out2), .out3(decoder_7_out3),
    .sel(WriteReg[3:2]), .en(decoder_1_out1));
  Decoder #(.select(2), .disabled(0)) decoder_8 (
    .out0(decoder_8_out0), .out1(decoder_8_out1), .out2(decoder_8_out2), .out3(decoder_8_out3),
    .sel(WriteReg[1:0]), .en(decoder_7_out0));
  Decoder #(.select(2), .disabled(0)) decoder_9 (
    .out0(decoder_9_out0), .out1(decoder_9_out1), .out2(decoder_9_out2), .out3(decoder_9_out3),
    .sel(WriteReg[1:0]), .en(decoder_7_out1));
  Decoder #(.select(2), .disabled(0)) decoder_10 (
    .out0(decoder_10_out0), .out1(decoder_10_out1), .out2(decoder_10_out2), .out3(decoder_10_out3),
    .sel(WriteReg[1:0]), .en(decoder_7_out2));
  Decoder #(.select(2), .disabled(0)) decoder_11 (
    .out0(decoder_11_out0), .out1(decoder_11_out1), .out2(decoder_11_out2), .out3(decoder_11_out3),
    .sel(WriteReg[1:0]), .en(decoder_7_out3));
  Register #(.width(32)) register_16 (.D(WriteData), .en(decoder_8_out0), .Q(register_16_q), .clk(Clk), .clr(Reset));
  Register #(.width(32)) register_17 (.D(WriteData), .en(decoder_8_out1), .Q(register_17_q), .clk(Clk), .clr(Reset));
  Register #(.width(32)) register_18 (.D(WriteData), .en(decoder_8_out2), .Q(register_18_q), .clk(Clk), .clr(Reset));
  Register #(.width(32)) register_19 (.D(WriteData), .en(decoder_8_out3), .Q(register_19_q), .clk(Clk), .clr(Reset));
  Register #(.width(32)) register_20 (.D(WriteData), .en(decoder_9_out0), .Q(register_20_q), .clk(Clk), .clr(Reset));
  Register #(.width(32)) register_21 (.D(WriteData), .en(decoder_9_out1), .Q(register_21_q), .clk(Clk), .clr(Reset));
  Register #(.width(32)) register_22 (.D(WriteData), .en(decoder_9_out2), .Q(register_22_q), .clk(Clk), .clr(Reset));
  Register #(.width(32)) register_23 (.D(WriteData), .en(decoder_9_out3), .Q(register_23_q), .clk(Clk), .clr(Reset));
  Register #(.width(32)) register_24 (.D(WriteData), .en(decoder_10_out0), .Q(register_24_q), .clk(Clk), .clr(Reset));
  Register #(.width(32)) register_25 (.D(WriteData), .en(decoder_10_out1), .Q(register_25_q), .clk(Clk), .clr(Reset));
  Register #(.width(32)) register_26 (.D(WriteData), .en(decoder_10_out2), .Q(register_26_q), .clk(Clk), .clr(Reset));
  Register #(.width(32)) register_27 (.D(WriteData), .en(decoder_10_out3), .Q(register_27_q), .clk(Clk), .clr(Reset));
  Register #(.width(32)) register_28 (.D(WriteData), .en(decoder_11_out0), .Q(register_28_q), .clk(Clk), .clr(Reset));
  Register #(.width(32)) register_29 (.D(WriteData), .en(decoder_11_out1), .Q(register_29_q), .clk(Clk), .clr(Reset));
  Register #(.width(32)) register_30 (.D(WriteData), .en(decoder_11_out2), .Q(register_30_q), .clk(Clk), .clr(Reset));
  Register #(.width(32)) register_31 (.D(WriteData), .en(decoder_11_out3), .Q(register_31_q), .clk(Clk), .clr(Reset));
  // Probe on register_16_q
  // Probe on register_17_q
  // Probe on register_18_q
  // Probe on register_19_q
  // Probe on register_20_q
  // Probe on register_21_q
  // Probe on register_22_q
  // Probe on register_23_q
  // Probe on register_24_q
  // Probe on register_25_q
  // Probe on register_26_q
  // Probe on register_27_q
  // Probe on register_28_q
  // Probe on register_29_q
  // Probe on register_30_q
  // Probe on register_31_q
  Multiplexer #(.width(32), .enable("false")) multiplexer_11 (
    .in0(multiplexer_10_out), .in1(multiplexer_21_out), .out(ReadData1), .sel(ReadReg1[4]));
  Multiplexer #(.width(32), .enable("false")) multiplexer_12 (
    .in0(multiplexer_9_out), .in1(multiplexer_22_out), .out(ReadData2), .sel(ReadReg2[4]));
  Multiplexer #(.select(2), .width(32), .enable("false")) multiplexer_13 (
    .in0(register_16_q), .in1(register_17_q), .in2(register_18_q), .in3(register_19_q),
    .out(multiplexer_13_out), .sel(ReadReg1[1:0]));
  Multiplexer #(.select(2), .width(32), .enable("false")) multiplexer_14 (
    .in0(register_20_q), .in1(register_21_q), .in2(register_22_q), .in3(register_23_q),
    .out(multiplexer_14_out), .sel(ReadReg1[1:0]));
  Multiplexer #(.select(2), .width(32), .enable("false")) multiplexer_15 (
    .in0(register_24_q), .in1(register_25_q), .in2(register_26_q), .in3(register_27_q),
    .out(multiplexer_15_out), .sel(ReadReg1[1:0]));
  Multiplexer #(.select(2), .width(32), .enable("false")) multiplexer_16 (
    .in0(register_28_q), .in1(register_29_q), .in2(register_30_q), .in3(register_31_q),
    .out(multiplexer_16_out), .sel(ReadReg1[1:0]));
  Multiplexer #(.select(2), .width(32), .enable("false")) multiplexer_17 (
    .in0(register_16_q), .in1(register_17_q), .in2(register_18_q), .in3(register_19_q),
    .out(multiplexer_17_out), .sel(ReadReg2[1:0]));
  Multiplexer #(.select(2), .width(32), .enable("false")) multiplexer_18 (
    .in0(register_20_q), .in1(register_21_q), .in2(register_22_q), .in3(register_23_q),
    .out(multiplexer_18_out), .sel(ReadReg2[1:0]));
  Multiplexer #(.select(2), .width(32), .enable("false")) multiplexer_19 (
    .in0(register_24_q), .in1(register_25_q), .in2(register_26_q), .in3(register_27_q),
    .out(multiplexer_19_out), .sel(ReadReg2[1:0]));
  Multiplexer #(.select(2), .width(32), .enable("false")) multiplexer_20 (
    .in0(register_28_q), .in1(register_29_q), .in2(register_30_q), .in3(register_31_q),
    .out(multiplexer_20_out), .sel(ReadReg2[1:0]));
  Multiplexer #(.select(2), .width(32), .enable("false")) multiplexer_21 (
    .in0(multiplexer_17_out), .in1(multiplexer_18_out), .in2(multiplexer_19_out), .in3(multiplexer_20_out),
    .out(multiplexer_21_out), .sel(ReadReg2[3:2]));
  Multiplexer #(.select(2), .width(32), .enable("false")) multiplexer_22 (
    .in0(multiplexer_13_out), .in1(multiplexer_14_out), .in2(multiplexer_15_out), .in3(multiplexer_16_out),
    .out(multiplexer_22_out), .sel(ReadReg1[3:2]));
endmodule
