// Logisim project mips.circ as structural Verilog: 5 circuits, main circuit main
module main (
);

  wire [31:0] instruction_memory_1_instruction;

  Instruction_Memory instruction_memory_1 (.Instruction(instruction_memory_1_instruction));  // open: Instruction_Addres
  Register_File Register_FIle ();  // open: Read_Register_2, Read_Register_2_2, Write_Register, Write_Data, CLK, Read_Data_1, Read_Data_2
  ALU ALU ();  // open: Cin, A, B, ZERO, RESULT, ALUCtrl
  Data_Memory Data_Memory ();  // open: A, WD, RD, MemWrite, MemRead
endmodule

module ALU (
  input  [2:0] ALUCtrl,
  input  Cin,
  input  [27:0] A,
  input  [27:0] B,
  output ZERO,
  output [31:0] RESULT
);

  wire [27:0] multiplexer_1_out, multiplexer_2_out, negator_1_out, negator_2_out;

  Multiplexer #(.width(28), .enable("false")) multiplexer_1 (
    .in0(A), .in1(negator_1_out), .out(multiplexer_1_out));  // open: sel
  Negator #(.width(28)) negator_1 (.in(A), .out(negator_1_out));
  Negator #(.width(28)) negator_2 (.in(B), .out(negator_2_out));
  Multiplexer #(.width(28), .enable("false")) multiplexer_2 (
    .in0(B), .in1(negator_2_out), .out(multiplexer_2_out));  // open: sel
  Adder #(.width(28)) adder_1 (.a(multiplexer_1_out), .b(multiplexer_2_out), .cin(Cin));  // open: out, cout
endmodule

module Register_File (
  input  [4:0] Read_Register_2,
  input  [4:0] Read_Register_2_2,
  input  [4:0] Write_Register,
  input  [31:0] Write_Data,
  input  CLK,
  output [31:0] Read_Data_1,
  output [31:0] Read_Data_2
);
endmodule

module Data_Memory (
  input  MemWrite,
  input  [31:0] A,
  input  [31:0] WD,
  input  MemRead,
  output [31:0] RD
);

  RAM #(.addrWidth(16)) ram_1 ();  // open: addr, data, sel, clk, ld, clr
  RAM #(.addrWidth(16)) ram_2 ();  // open: addr, data, sel, clk, ld, clr
endmodule

module Instruction_Memory (
  input  [31:0] Instruction_Addres,
  output [31:0] Instruction
);
endmodule
